# Fritzing sketch Tugas2 (saved by Fritzing 0.8.7b)
breadboards: 1

parts:
  LED1 = LED - 5mm [color="Red (633nm)" package="5 mm [THT]"]
  Raspberry_Pi_B_rev1 = Raspberry Pi B rev1
  LED2 = LED - 5mm [color="Red (633nm)" package="5 mm [THT]"]
  LED3 = LED - 5mm [color="Red (633nm)" package="5 mm [THT]"]

nets:
  N1: LED1.cathode, Raspberry_Pi_B_rev1.GND, LED2.cathode, LED3.cathode
  N2: LED1.anode, Raspberry_Pi_B_rev1.GPIO_18
  N3: Raspberry_Pi_B_rev1.GPIO_24, LED3.anode
  N4: Raspberry_Pi_B_rev1.GPIO_25, LED2.anode
